# Fritzing sketch six_button_module (saved by Fritzing 0.9.6b)
circuit board: 7.12906cm x 6.3802cm
breadboards: 1

parts:
  R1 = Resistor [tolerance=±1% power=0.25 resistance=330 package=THT]
  R3 = Resistor [tolerance=±1% power=0.25 resistance=2140 package=THT]
  R4 = Resistor [tolerance=±5% power=0.25 resistance=3.6k package=THT]
  R5 = Resistor [tolerance=±5% power=0.25 resistance=7.2k package=THT]
  R6 = Resistor [tolerance=±5% power=0.25 resistance=20.5k package=THT]
  Rv = Resistor [tolerance=±5% power=0.25 resistance=2.7k package=THT]
  S2 = Pushbutton [package="[THT]"]
  S3 = Pushbutton [package="[THT]"]
  S4 = Pushbutton [package="[THT]"]
  S5 = Pushbutton [package="[THT]"]
  S1 = Pushbutton [package="[THT]"]
  S6 = Pushbutton [package="[THT]"]
  R2 = Resistor [tolerance=±1% power=0.25 resistance=1070 package=THT]
  J1 = molex pin header, 3 pins [form=molex]

nets:
  N1: R1.Pin_0, R3.Pin_0, R4.Pin_0, R5.Pin_0, R6.Pin_0, Rv.Pin_1, R2.Pin_0, J1.pin2
  N2: R1.Pin_1, S1.Pin_3, S1.Pin_4
  N3: R3.Pin_1, S3.Pin_3, S3.Pin_4
  N4: R4.Pin_1, S4.Pin_3, S4.Pin_4
  N5: R5.Pin_1, S5.Pin_3, S5.Pin_4
  N6: R6.Pin_1, S6.Pin_3, S6.Pin_4
  3.3V: Rv.Pin_0, J1.pin1
  GND: S2.Pin_1, S2.Pin_2, S3.Pin_1, S3.Pin_2, S4.Pin_1, S4.Pin_2, S5.Pin_1, S5.Pin_2, S1.Pin_1, S1.Pin_2, S6.Pin_1, S6.Pin_2, J1.pin3
  N7: S2.Pin_3, S2.Pin_4, R2.Pin_1

notes:
  6 Button Module
  Vcc
  Ua
  GND
  12/2022
  6 Button
  Module
  P. Glass
